// Logisim project Circuitos Sequenciais - Flip-flops.circ as structural Verilog: 5 circuits, main circuit Contador assíncrono decrescente
module \Contador_assíncrono_decrescente  (
  input  clock,
  input  data,
  input  clear,
  output out_4,
  output out_5,
  output out_6,
  output out_7,
  output out_8
);

  J_K_Flip_Flop j_k_ff_1 (.J(data), .clk(out_5), .K(data), .Qn(out_4), .reset(clear));  // open: Q, preset, en
  J_K_Flip_Flop j_k_ff_2 (.J(data), .clk(out_6), .K(data), .Qn(out_5), .reset(clear));  // open: Q, preset, en
  J_K_Flip_Flop j_k_ff_3 (.J(data), .clk(out_7), .K(data), .Qn(out_6), .reset(clear));  // open: Q, preset, en
  J_K_Flip_Flop j_k_ff_4 (.J(data), .clk(out_8), .K(data), .Qn(out_7), .reset(clear));  // open: Q, preset, en
  J_K_Flip_Flop j_k_ff_5 (.J(data), .clk(clock), .K(data), .Qn(out_8), .reset(clear));  // open: Q, preset, en
endmodule

module \Contador_assíncrono_crescente  (
  input  clock,
  input  data,
  input  clear,
  output out_4,
  output out_5,
  output out_6,
  output out_7,
  output out_8
);

  wire j_k_ff_2_qn, j_k_ff_3_qn, j_k_ff_4_qn, j_k_ff_5_qn;

  J_K_Flip_Flop j_k_ff_1 (.J(data), .clk(j_k_ff_2_qn), .K(data), .Q(out_4), .reset(clear));  // open: Qn, preset, en
  J_K_Flip_Flop j_k_ff_2 (
    .J(data), .clk(j_k_ff_3_qn), .K(data), .Q(out_5), .Qn(j_k_ff_2_qn), .reset(clear));  // open: preset, en
  J_K_Flip_Flop j_k_ff_3 (
    .J(data), .clk(j_k_ff_4_qn), .K(data), .Q(out_6), .Qn(j_k_ff_3_qn), .reset(clear));  // open: preset, en
  J_K_Flip_Flop j_k_ff_4 (
    .J(data), .clk(j_k_ff_5_qn), .K(data), .Q(out_7), .Qn(j_k_ff_4_qn), .reset(clear));  // open: preset, en
  J_K_Flip_Flop j_k_ff_5 (
    .J(data), .clk(clock), .K(data), .Q(out_8), .Qn(j_k_ff_5_qn), .reset(clear));  // open: preset, en
endmodule

module \Contador_Decádico_Decrescente  (
  input  data,
  input  clock,
  input  clear,
  output [3:0] out_4
);

  wire and_1_out, j_k_ff_1_qn, j_k_ff_2_qn, j_k_ff_3_qn, j_k_ff_4_qn, not_1_out, or_1_out;

  J_K_Flip_Flop j_k_ff_1 (
    .J(data), .clk(clock), .K(data), .Q(out_4[0]), .Qn(j_k_ff_1_qn), .preset(or_1_out), .reset(clear));  // open: en
  not not_1 (not_1_out, data);
  or or_1 (or_1_out, not_1_out, and_1_out);
  and and_1 (and_1_out, j_k_ff_1_qn, j_k_ff_2_qn, j_k_ff_3_qn, j_k_ff_4_qn);
  J_K_Flip_Flop j_k_ff_2 (
    .J(data), .clk(out_4[0]), .K(data), .Q(out_4[1]), .Qn(j_k_ff_2_qn), .preset(or_1_out), .reset(clear));  // open: en
  J_K_Flip_Flop j_k_ff_3 (
    .J(data), .clk(out_4[1]), .K(data), .Q(out_4[2]), .Qn(j_k_ff_3_qn), .preset(or_1_out), .reset(clear));  // open: en
  J_K_Flip_Flop j_k_ff_4 (
    .J(data), .clk(out_4[2]), .K(data), .Q(out_4[3]), .Qn(j_k_ff_4_qn), .preset(or_1_out), .reset(clear));  // open: en
endmodule

module \Contador_Decádio_Crescente  (
  input  data,
  input  clock,
  input  clear,
  output [3:0] out_4
);

  wire and_1_out, j_k_ff_1_qn, j_k_ff_2_qn, j_k_ff_3_qn, nand_1_out, not_1_out, not_2_out;

  nand nand_1 (nand_1_out, clear, not_1_out);
  not not_1 (not_1_out, and_1_out);
  and and_1 (and_1_out, out_4[0], out_4[1], not_2_out, out_4[3]);
  J_K_Flip_Flop j_k_ff_1 (
    .J(data), .clk(clock), .K(data), .Q(out_4[0]), .Qn(j_k_ff_1_qn), .reset(nand_1_out));  // open: preset, en
  not not_2 (not_2_out, out_4[2]);
  J_K_Flip_Flop j_k_ff_2 (
    .J(data), .clk(j_k_ff_1_qn), .K(data), .Q(out_4[1]), .Qn(j_k_ff_2_qn), .reset(nand_1_out));  // open: preset, en
  J_K_Flip_Flop j_k_ff_3 (
    .J(data), .clk(j_k_ff_2_qn), .K(data), .Q(out_4[2]), .Qn(j_k_ff_3_qn), .reset(nand_1_out));  // open: preset, en
  J_K_Flip_Flop j_k_ff_4 (
    .J(data), .clk(j_k_ff_3_qn), .K(data), .Q(out_4[3]), .reset(nand_1_out));  // open: Qn, preset, en
endmodule

module Contador_sincrono_base_8 (
  input  data,
  input  clear,
  output [2:0] out_3
);

  wire and_1_out, clock_out;

  Clock clock (.out(clock_out));
  T_Flip_Flop t_ff_1 (.clk(clock_out), .T(data), .Q(out_3[0]), .reset(clear));  // open: Qn, preset, en
  T_Flip_Flop t_ff_2 (.clk(clock_out), .T(out_3[0]), .Q(out_3[1]), .reset(clear));  // open: Qn, preset, en
  and and_1 (and_1_out, out_3[1], out_3[0]);
  T_Flip_Flop t_ff_3 (.clk(clock_out), .T(and_1_out), .Q(out_3[2]), .reset(clear));  // open: Qn, preset, en
endmodule
